# Fritzing sketch main (saved by Fritzing 0.9.3b)
breadboards: 1

parts:
  BLUETOOTH = Bluetooth HC-06
  ARDUINO = Arduino Uno (Rev3) - ICSP
  RGB_SENSOR = TCS230 Color Sensor [part_number=101209]
  LINE_TRACKER = KY-033 Tracing Black White Line Hunting Sensor Module For Arduino
  MOTOR_DC = DC Motor

nets:
  N1: BLUETOOTH.RXD, ARDUINO.D1/TX
  N2: BLUETOOTH.TXD, ARDUINO.D0/RX
  GND: BLUETOOTH.GND, ARDUINO.GND, RGB_SENSOR.Gnd, RGB_SENSOR.OE, LINE_TRACKER.GND, MOTOR_DC.pin_1
  VCC: BLUETOOTH.VCC, ARDUINO.5V, RGB_SENSOR.Vcc, LINE_TRACKER.V+
  N3: ARDUINO.A3, LINE_TRACKER.S
  N4: ARDUINO.D8, RGB_SENSOR.S0
  N5: ARDUINO.D9_PWM, RGB_SENSOR.S1
  N6: ARDUINO.D10_PWM/SS, RGB_SENSOR.Out
  N7: ARDUINO.D11_PWM/MOSI, RGB_SENSOR.S3
  N8: ARDUINO.D12/MISO, RGB_SENSOR.S2
  N9: ARDUINO.D7, MOTOR_DC.pin_2

custom parts:
  TCS230 Color Sensor: TCS230
  KY-033 Tracing Black White Line Hunting Sensor Module For Arduino: Tracing Black White Line Hunting Sensor Module For Arduino Description: This is KY-033 tracking sensor. The KY-033 measures the intensity of infrared radiation and delivers it as an analog output voltage. Features: Operating voltage: 2.5 - 12V(cannot over12V) working current: 18mA-20mA at 5V Enhanced accuracy Documents: http://www.vishay.com/docs/83760/tcrt5000.pdf

// code stored in the sketch: arduino.ino
int led = 13;

void setup () {
	Serial.begin(9600);
	pinMode(led, OUTPUT);
}

void loop () {
	delay(800);
	digitalWrite(led, HIGH);
	delay(800);
	digitalWrite(led, LOW);
}
